// Logisim project logisim.circ as structural Verilog: 3 circuits, main circuit main
module main (
);

  wire clock_1_out;
  wire [23:0] cpu_1_addr;
  wire [63:0] rom_1_data;

  Clock clock_1 (.out(clock_1_out));
  ROM #(.addrWidth(4), .dataWidth(64)) rom_1 (.addr(cpu_1_addr[3:0]), .data(rom_1_data));
  CPU cpu_1 (.CLK(clock_1_out), .DIN(rom_1_data), .ADDR(cpu_1_addr));  // open: R, WE, DOUT, OE

  // Notes on the sheet:
  //   contents of rom_1 (hex, n*v repeats v):
  //   3 1 2 2 0 1 4 0 6 1
endmodule

module CPU (
  input  CLK,
  input  R,
  input  [63:0] DIN,
  output [23:0] ADDR,
  output WE,
  output [63:0] DOUT,
  output OE
);

  wire ADDRLOAD, ALOAD, ALUOUT, BLOAD, comparator_1_eq, controlled_buffer_11_out, counter_1_carry,
       decoder_1_out0, decoder_1_out1, decoder_1_out2, decoder_1_out3, decoder_2_out0, decoder_2_out1,
       decoder_2_out2, decoder_2_out3, HLT, IR0LOAD, IR1LOAD, IR1OUT, IR2LOAD, IR2OUT, LOADGP, not_1_out,
       OUTGP, PCLOAD, PCOUT, s_r_ff_1_qn;
  wire [1:0] multiplexer_1_out, multiplexer_2_out, rom_1_data_2, rom_1_data_3, undriven_2;
  wire [2:0] rom_1_data;
  wire [12:0] counter_1_q;
  wire [18:0] controlled_buffer_1_out_2;
  wire [19:0] undriven;
  wire [20:0] controlled_buffer_1_out_3;
  wire [23:0] adder_1_out, controlled_buffer_1_out, counter_2_q, multiplier_1_out, subtractor_1_out;
  wire [63:0] alu_1_o, register_1_q, register_2_q, register_3_q, register_4_q, register_6_q, register_7_q,
       register_8_q, register_9_q;

  Counter #(.max('hf), .width(4)) counter_1 (
    .clr(R), .clk(not_1_out), .carry(counter_1_carry), .Q(counter_1_q[3:0]));  // open: load, up, count, D
  not not_1 (not_1_out, controlled_buffer_11_out);
  ROM #(.addrWidth(13), .dataWidth(22)) rom_1 (
    .addr(counter_1_q),
    .data({HLT, WE, OE, PCOUT, PCLOAD, ADDRLOAD, IR2LOAD, IR1LOAD, IR0LOAD, ALUOUT, rom_1_data_2, rom_1_data_3, IR2OUT, IR1OUT, BLOAD, ALOAD, LOADGP, rom_1_data[2], OUTGP, rom_1_data[0]}));
  assign {controlled_buffer_1_out_3, controlled_buffer_1_out_2, controlled_buffer_1_out} = decoder_1_out0 ? register_1_q : 64'bz;  // Controlled_Buffer controlled_buffer_1
  Register #(.width(64)) register_1 (
    .D({controlled_buffer_1_out_3, controlled_buffer_1_out_2, controlled_buffer_1_out}), .en(decoder_2_out0),
    .clk(controlled_buffer_11_out), .Q(register_1_q), .clr(R));
  assign {controlled_buffer_1_out_3, controlled_buffer_1_out_2, controlled_buffer_1_out} = decoder_1_out1 ? register_2_q : 64'bz;  // Controlled_Buffer controlled_buffer_2
  Register #(.width(64)) register_2 (
    .D({controlled_buffer_1_out_3, controlled_buffer_1_out_2, controlled_buffer_1_out}), .en(decoder_2_out1),
    .clk(controlled_buffer_11_out), .Q(register_2_q), .clr(R));
  assign {controlled_buffer_1_out_3, controlled_buffer_1_out_2, controlled_buffer_1_out} = decoder_1_out2 ? register_3_q : 64'bz;  // Controlled_Buffer controlled_buffer_3
  Register #(.width(64)) register_3 (
    .D({controlled_buffer_1_out_3, controlled_buffer_1_out_2, controlled_buffer_1_out}), .en(decoder_2_out2),
    .clk(controlled_buffer_11_out), .Q(register_3_q), .clr(R));
  assign {controlled_buffer_1_out_3, controlled_buffer_1_out_2, controlled_buffer_1_out} = decoder_1_out3 ? register_4_q : 64'bz;  // Controlled_Buffer controlled_buffer_4
  Register #(.width(64)) register_4 (
    .D({controlled_buffer_1_out_3, controlled_buffer_1_out_2, controlled_buffer_1_out}), .en(decoder_2_out3),
    .clk(controlled_buffer_11_out), .Q(register_4_q), .clr(R));
  Register register_5 (
    .D(controlled_buffer_1_out[7:0]), .en(IR0LOAD), .clk(controlled_buffer_11_out), .Q(counter_1_q[11:4]),
    .clr(R));
  Register #(.width(64)) register_6 (
    .D({controlled_buffer_1_out_3, controlled_buffer_1_out_2, controlled_buffer_1_out}), .en(IR1LOAD),
    .clk(controlled_buffer_11_out), .Q(register_6_q), .clr(R));
  Register #(.width(64)) register_7 (
    .D({controlled_buffer_1_out_3, controlled_buffer_1_out_2, controlled_buffer_1_out}), .en(IR2LOAD),
    .clk(controlled_buffer_11_out), .Q(register_7_q), .clr(R));
  Register #(.width(64)) register_8 (
    .D({controlled_buffer_1_out_3, controlled_buffer_1_out_2, controlled_buffer_1_out}), .en(ALOAD),
    .clk(controlled_buffer_11_out), .Q(register_8_q), .clr(R));
  Register #(.width(64)) register_9 (
    .D({controlled_buffer_1_out_3, controlled_buffer_1_out_2, controlled_buffer_1_out}), .en(BLOAD),
    .clk(controlled_buffer_11_out), .Q(register_9_q), .clr(R));
  assign {controlled_buffer_1_out_3, controlled_buffer_1_out_2, controlled_buffer_1_out} = PCOUT ? {{40{1'b0}}, subtractor_1_out} : 64'bz;  // Controlled_Buffer controlled_buffer_5
  Register #(.width(24)) register_10 (
    .D(controlled_buffer_1_out), .en(ADDRLOAD), .clk(controlled_buffer_11_out), .Q(ADDR), .clr(R));
  assign {controlled_buffer_1_out_3, controlled_buffer_1_out_2, controlled_buffer_1_out} = IR1OUT ? register_6_q : 64'bz;  // Controlled_Buffer controlled_buffer_6
  assign {controlled_buffer_1_out_3, controlled_buffer_1_out_2, controlled_buffer_1_out} = IR2OUT ? register_7_q : 64'bz;  // Controlled_Buffer controlled_buffer_7
  assign {controlled_buffer_1_out_3, controlled_buffer_1_out_2, controlled_buffer_1_out} = ALUOUT ? alu_1_o : 64'bz;  // Controlled_Buffer controlled_buffer_8
  assign DOUT = WE ? {controlled_buffer_1_out_3, controlled_buffer_1_out_2, controlled_buffer_1_out} : 64'bz;  // Controlled_Buffer controlled_buffer_9
  assign {controlled_buffer_1_out_3, controlled_buffer_1_out_2, controlled_buffer_1_out} = OE ? DIN : 64'bz;  // Controlled_Buffer controlled_buffer_10
  Multiplexer #(.width(2)) multiplexer_1 (
    .in0(register_6_q[1:0]), .in1(register_7_q[1:0]), .out(multiplexer_1_out), .sel(rom_1_data[0]));
  Multiplexer #(.width(2)) multiplexer_2 (
    .in0(register_6_q[1:0]), .in1(register_7_q[1:0]), .out(multiplexer_2_out), .sel(rom_1_data[2]));
  assign controlled_buffer_11_out = s_r_ff_1_qn ? CLK : 1'bz;  // Controlled_Buffer controlled_buffer_11
  S_R_Flip_Flop #(.trigger("high")) s_r_ff_1 (.S(HLT), .R(R), .clk(1'b1), .Qn(s_r_ff_1_qn));  // open: Q, reset, preset
  Decoder #(.select(2)) decoder_1 (
    .out0(decoder_1_out0), .out1(decoder_1_out1), .out2(decoder_1_out2), .out3(decoder_1_out3),
    .sel(multiplexer_1_out), .en(OUTGP));
  Decoder #(.select(2)) decoder_2 (
    .out0(decoder_2_out0), .out1(decoder_2_out1), .out2(decoder_2_out2), .out3(decoder_2_out3),
    .sel(multiplexer_2_out), .en(LOADGP));
  Hex_Digit_Display hex_digit_display_1 (.value({2'b00, undriven_2}));  // open: dp
  ALU alu_1 (.A(register_8_q), .B(register_9_q), .OP(rom_1_data_2), .O(alu_1_o));
  Hex_Digit_Display hex_digit_display_2 (.value(undriven[19:16]));  // open: dp
  Hex_Digit_Display hex_digit_display_3 (.value(undriven[15:12]));  // open: dp
  // DipSwitch #(.number(22)) dipswitch_1: pin names not known
  Hex_Digit_Display hex_digit_display_4 (.value(undriven[11:8]));  // open: dp
  Hex_Digit_Display hex_digit_display_5 (.value(undriven[7:4]));  // open: dp
  Counter #(.max('hffffff), .width(24)) counter_2 (
    .clr(R), .load(PCLOAD), .up(1'b1), .count(counter_1_carry), .clk(controlled_buffer_11_out),
    .D(controlled_buffer_1_out), .Q(counter_2_q));  // open: carry
  Hex_Digit_Display hex_digit_display_6 (.value(undriven[3:0]));  // open: dp
  Register #(.width(1)) register_11 (
    .D(comparator_1_eq), .en(ALUOUT), .clk(controlled_buffer_11_out), .Q(counter_1_q[12]), .clr(R));
  Comparator #(.width(64)) comparator_1 (.a(alu_1_o), .b({64{1'b0}}), .eq(comparator_1_eq));  // open: gt, lt
  Adder #(.width(24)) adder_1 (.a(counter_2_q), .b(24'h1), .out(adder_1_out));  // open: cin, cout
  Multiplier #(.width(24)) multiplier_1 (.a(adder_1_out), .b(24'h3), .out(multiplier_1_out));  // open: cin, cout
  Subtractor #(.width(24)) subtractor_1 (
    .a(multiplier_1_out), .b({{22{1'b0}}, rom_1_data_3}), .out(subtractor_1_out));  // open: bin, bout

  // Other names for the same wires on the sheet: MEMOUT = OE; MEMLOAD = WE

  // Notes on the sheet:
  //   contents of rom_1 (hex, n*v repeats v):
  //   50300 82000 14*0 50300 82000 200000 13*0 50300 82000 50200 84000 50100 88000 b 9*0 50300 82000 50200
  //   84000 50100 88000 88 9*0 50300 82000 50200 84000 50100 88000 10080 80008
  //   Instruction Registers
  //   A Register
  //   B Register
  //   General Purpose 0
  //   General Purpose 1
  //   General Purpose 2
  //   General Purpose 3
endmodule

module ALU (
  input  [63:0] A,
  input  [63:0] B,
  input  [1:0] OP,
  output [63:0] O
);

  wire subtractor_1_bout;
  wire [63:0] adder_1_out, divider_1_out, multiplexer_1_out, multiplier_1_out, negator_1_out,
       subtractor_1_out;

  Adder #(.width(64)) adder_1 (.a(A), .b(B), .out(adder_1_out));  // open: cin, cout
  Subtractor #(.width(64)) subtractor_1 (.a(A), .b(B), .out(subtractor_1_out), .bout(subtractor_1_bout));  // open: bin
  Negator #(.width(64)) negator_1 (.in(subtractor_1_out), .out(negator_1_out));
  Multiplier #(.mode("twosComplement"), .width(64)) multiplier_1 (
    .a(A), .b(B), .out(multiplier_1_out));  // open: cin, cout
  Divider #(.mode("twosComplement"), .width(64)) divider_1 (.a(A), .b(B), .out(divider_1_out));  // open: upper, rem
  Multiplexer #(.width(64)) multiplexer_1 (
    .in0(subtractor_1_out), .in1(negator_1_out), .out(multiplexer_1_out), .sel(subtractor_1_bout));
  Multiplexer #(.select(2), .width(64)) multiplexer_2 (
    .in0(adder_1_out), .in1(multiplexer_1_out), .in2(multiplier_1_out), .in3(divider_1_out), .out(O), .sel(OP));
endmodule
